# Fritzing sketch cabling_scheme_nfc_esp (saved by Fritzing 0.9.9b)
breadboards: 1

parts:
  Composant1 = RFID-RC522-v2
  Composant3 = Arduino Mega 2560 (Rev3)
  U2 = ESP8266 WiFi Module [part_number=ESP8266]

nets:
  N1: Composant1.SDA, Composant3.D9_PWM
  N2: Composant1.SCK, Composant3.D52
  N3: Composant1.MOSI, Composant3.D51
  N4: Composant1.MISO, Composant3.D50
  GND: Composant1.GND, Composant3.GND, U2.GND
  N5: Composant1.RST, Composant3.D8_PWM
  3.3V: Composant1.3.3V, Composant3.3V3, U2.VCC, U2.CH_PD
  N6: Composant3.D15/RX3, U2.RXD
  N7: Composant3.D14/TX3, U2.TXD

custom parts:
  RFID-RC522-v2: A simple China made RFID-RC522 Reader; do check the pin labels, as this is a MFRC522 based clone.
